// Logisim project Compute.circ as structural Verilog: 4 circuits, main circuit main
module main (
  input  in_1,
  input  in_2,
  input  in_3,
  input  Load,
  input  Set
);

  wire CLK, NextLine, SaveLine, SEL, SplitLine, tickcounter_1_t3, tickcounter_1_t4;

  TickCounter tickcounter_1 (
    .Clock(CLK), .Enable(in_2), .T0(NextLine), .T4(tickcounter_1_t4), .T3(tickcounter_1_t3), .T2(SaveLine),
    .T1(SplitLine));  // open: T15, T14, T13, T12, T11, T10, T9, T8, T7, T6, T5
  Clock clock_1 (.out(CLK));
  or or_1 (SEL, Load, Set);

  // Other names for the same wires on the sheet: CLR = in_1; RUN = in_2; STR = Load
endmodule

module TickCounter (
  input  Clock,
  input  Enable,
  output T9,
  output T10,
  output T8,
  output T11,
  output T7,
  output T12,
  output T6,
  output T13,
  output T5,
  output T14,
  output T4,
  output T15,
  output T3,
  output T0,
  output T2,
  output T1
);

  wire not_1_out, O1, O2, O3, O4;

  T_Flip_Flop t_ff_1 (.clk(Clock), .T(1'b1), .Q(O1), .reset(not_1_out), .en(Enable));  // open: Qn, preset
  T_Flip_Flop t_ff_2 (.clk(O1), .T(1'b1), .Q(O2), .reset(not_1_out), .en(Enable));  // open: Qn, preset
  T_Flip_Flop t_ff_3 (.clk(O2), .T(1'b1), .Q(O3), .reset(not_1_out), .en(Enable));  // open: Qn, preset
  T_Flip_Flop t_ff_4 (.clk(O3), .T(1'b1), .Q(O4), .reset(not_1_out), .en(Enable));  // open: Qn, preset
  not not_1 (not_1_out, Enable);
  Demultiplexer #(.select(4), .disabled(0), .enable("false")) demultiplexer_1 (
    .out0(T0), .out1(T15), .out2(T14), .out3(T13), .out4(T12), .out5(T11), .out6(T10), .out7(T9), .out8(T8),
    .out9(T7), .out10(T6), .out11(T5), .out12(T4), .out13(T3), .out14(T2), .out15(T1), .in(Enable),
    .sel({O4, O3, O2, O1}));

  // Other names for the same wires on the sheet: CK = Clock; EN = Enable
endmodule

module _8BitIncrement (
  input  Clock,
  input  Enable,
  input  [7:0] Set,
  output [7:0] out_4
);

  wire not_1_out, not_2_out, not_3_out, not_4_out, not_5_out, not_7_out, not_8_out, not_9_out, O1, O2, O3,
       O4, O5, O6, O7, O8;
  wire [7:0] controlled_inverter_1_out;

  assign controlled_inverter_1_out = Clock ? ~Set : 8'bz;  // Controlled_Inverter controlled_inverter_1
  T_Flip_Flop t_ff_1 (
    .clk(Clock), .T(1'b1), .Q(O1), .preset(controlled_inverter_1_out[0]), .reset(not_1_out), .en(Enable));  // open: Qn
  not not_1 (not_1_out, controlled_inverter_1_out[0]);
  T_Flip_Flop t_ff_2 (
    .clk(O1), .T(1'b1), .Q(O2), .preset(controlled_inverter_1_out[1]), .reset(not_2_out), .en(Enable));  // open: Qn
  not not_2 (not_2_out, controlled_inverter_1_out[1]);
  T_Flip_Flop t_ff_3 (
    .clk(O2), .T(1'b1), .Q(O3), .preset(controlled_inverter_1_out[2]), .reset(not_3_out), .en(Enable));  // open: Qn
  not not_3 (not_3_out, controlled_inverter_1_out[2]);
  T_Flip_Flop t_ff_4 (
    .clk(O3), .T(1'b1), .Q(O4), .preset(controlled_inverter_1_out[3]), .reset(not_4_out), .en(Enable));  // open: Qn
  not not_4 (not_4_out, controlled_inverter_1_out[3]);
  T_Flip_Flop t_ff_5 (
    .clk(O4), .T(1'b1), .Q(O5), .preset(controlled_inverter_1_out[4]), .reset(not_5_out), .en(Enable));  // open: Qn
  not not_5 (not_5_out, controlled_inverter_1_out[4]);
  // NOT_Gate not_6 is placed but not wired
  T_Flip_Flop t_ff_6 (
    .clk(O5), .T(1'b1), .Q(O6), .preset(controlled_inverter_1_out[5]), .reset(not_7_out), .en(Enable));  // open: Qn
  not not_7 (not_7_out, controlled_inverter_1_out[5]);
  T_Flip_Flop t_ff_7 (
    .clk(O6), .T(1'b1), .Q(O7), .preset(controlled_inverter_1_out[6]), .reset(not_8_out), .en(Enable));  // open: Qn
  not not_8 (not_8_out, controlled_inverter_1_out[6]);
  T_Flip_Flop t_ff_8 (
    .clk(O7), .T(1'b1), .Q(O8), .preset(controlled_inverter_1_out[7]), .reset(not_9_out), .en(Enable));  // open: Qn
  not not_9 (not_9_out, controlled_inverter_1_out[7]);
  assign out_4 = ~{O8, O7, O6, O5, O4, O3, O2, O1};  // NOT_Gate not_10, 8 bits wide

  // Other names for the same wires on the sheet: CK = Clock; EN = Enable; ST[7:0] = Set
endmodule

module CommandController (
  input  Clock,
  input  in_2,
  input  [7:0] Set_IC
);

  wire [7:0] controlled_buffer_1_out, n8bitincrement_1_out_4, rom_1_data;

  _8BitIncrement u_8bitincrement_1 (.Clock(Clock), .Enable(in_2), .out_4(n8bitincrement_1_out_4), .Set(Set_IC));
  ROM rom_1 (.addr(n8bitincrement_1_out_4), .data(rom_1_data), .sel(in_2));
  assign controlled_buffer_1_out = in_2 ? rom_1_data : 8'bz;  // Controlled_Buffer controlled_buffer_1
  Register #(.width(5)) register_1 (.D(controlled_buffer_1_out[4:0]), .en(in_2), .clk(Clock));  // open: Q, clr
  Register #(.width(3)) register_2 (.D(controlled_buffer_1_out[7:5]), .en(in_2), .clk(Clock));  // open: Q, clr

  // Other names for the same wires on the sheet: CLK = Clock; ENB = in_2; SIC[7:0] = Set_IC

  // Notes on the sheet:
  //   contents of rom_1 (hex, n*v repeats v):
  //   aa 0 aa 29*0 11
endmodule
