// Logisim project Yuh.circ as structural Verilog
module MEM___RegisterController (
  input  Clock,
  input  Clear,
  input  [7:0] DataIn,
  input  Read_Write,
  input  Enable,
  input  [3:0] Register,
  output [7:0] out_7
);

  wire R0, R1, R2, R3, R4, R5, R6, R7, R8, R9, R10, R11, R12, R13, R14, R15;
  wire [7:0] controlled_buffer_1_out, controlled_buffer_2_out, controlled_buffer_3_out,
       controlled_buffer_4_out, controlled_buffer_5_out, controlled_buffer_6_out, controlled_buffer_7_out,
       controlled_buffer_8_out, controlled_buffer_18_out, controlled_buffer_20_out, controlled_buffer_21_out,
       controlled_buffer_24_out, controlled_buffer_26_out, controlled_buffer_27_out,
       controlled_buffer_30_out, controlled_buffer_31_out, register_1_q, register_2_q, register_3_q,
       register_4_q, register_5_q, register_6_q, register_7_q, register_8_q, register_9_q, register_10_q,
       register_11_q, register_12_q, register_13_q, register_14_q, register_15_q, register_16_q;

  Demultiplexer #(.select(4)) demultiplexer_1 (
    .out0(R0), .out1(R1), .out2(R2), .out3(R3), .out4(R4), .out5(R5), .out6(R6), .out7(R7), .out8(R8),
    .out9(R9), .out10(R10), .out11(R11), .out12(R12), .out13(R13), .out14(R14), .out15(R15), .in(1'b1),
    .sel(Register), .en(Enable));
  assign controlled_buffer_1_out = R0 ? DataIn : 8'bz;  // Controlled_Buffer controlled_buffer_1
  Register register_1 (.D(controlled_buffer_1_out), .en(Read_Write), .Q(register_1_q), .clk(Clock), .clr(Clear));
  assign controlled_buffer_2_out = R1 ? DataIn : 8'bz;  // Controlled_Buffer controlled_buffer_2
  Register register_2 (.D(controlled_buffer_2_out), .en(Read_Write), .Q(register_2_q), .clk(Clock), .clr(Clear));
  assign controlled_buffer_3_out = R2 ? DataIn : 8'bz;  // Controlled_Buffer controlled_buffer_3
  Register register_3 (.D(controlled_buffer_3_out), .en(Read_Write), .Q(register_3_q), .clk(Clock), .clr(Clear));
  assign controlled_buffer_4_out = R3 ? DataIn : 8'bz;  // Controlled_Buffer controlled_buffer_4
  Register register_4 (.D(controlled_buffer_4_out), .en(Read_Write), .Q(register_4_q), .clk(Clock), .clr(Clear));
  Register register_5 (.D(controlled_buffer_5_out), .en(Read_Write), .Q(register_5_q), .clk(Clock), .clr(Clear));
  assign controlled_buffer_5_out = R4 ? DataIn : 8'bz;  // Controlled_Buffer controlled_buffer_5
  assign controlled_buffer_6_out = R5 ? DataIn : 8'bz;  // Controlled_Buffer controlled_buffer_6
  Register register_6 (.D(controlled_buffer_6_out), .en(Read_Write), .Q(register_6_q), .clk(Clock), .clr(Clear));
  Register register_7 (.D(controlled_buffer_7_out), .en(Read_Write), .Q(register_7_q), .clk(Clock), .clr(Clear));
  assign controlled_buffer_7_out = R6 ? DataIn : 8'bz;  // Controlled_Buffer controlled_buffer_7
  assign controlled_buffer_8_out = R7 ? DataIn : 8'bz;  // Controlled_Buffer controlled_buffer_8
  Register register_8 (.D(controlled_buffer_8_out), .en(Read_Write), .Q(register_8_q), .clk(Clock), .clr(Clear));
  assign out_7 = R0 ? register_1_q : 8'bz;  // Controlled_Buffer controlled_buffer_9
  assign out_7 = R1 ? register_2_q : 8'bz;  // Controlled_Buffer controlled_buffer_10
  assign out_7 = R2 ? register_3_q : 8'bz;  // Controlled_Buffer controlled_buffer_11
  assign out_7 = R3 ? register_4_q : 8'bz;  // Controlled_Buffer controlled_buffer_12
  assign out_7 = R4 ? register_5_q : 8'bz;  // Controlled_Buffer controlled_buffer_13
  assign out_7 = R5 ? register_6_q : 8'bz;  // Controlled_Buffer controlled_buffer_14
  assign out_7 = R6 ? register_7_q : 8'bz;  // Controlled_Buffer controlled_buffer_15
  assign out_7 = R7 ? register_8_q : 8'bz;  // Controlled_Buffer controlled_buffer_16
  Register register_9 (.D(controlled_buffer_18_out), .en(Read_Write), .Q(register_9_q), .clk(Clock), .clr(Clear));
  assign out_7 = R8 ? register_9_q : 8'bz;  // Controlled_Buffer controlled_buffer_17
  assign controlled_buffer_18_out = R8 ? DataIn : 8'bz;  // Controlled_Buffer controlled_buffer_18
  assign out_7 = R9 ? register_10_q : 8'bz;  // Controlled_Buffer controlled_buffer_19
  Register register_10 (.D(controlled_buffer_20_out), .en(Read_Write), .Q(register_10_q), .clk(Clock), .clr(Clear));
  assign controlled_buffer_20_out = R9 ? DataIn : 8'bz;  // Controlled_Buffer controlled_buffer_20
  Register register_11 (.D(controlled_buffer_21_out), .en(Read_Write), .Q(register_11_q), .clk(Clock), .clr(Clear));
  assign controlled_buffer_21_out = R10 ? DataIn : 8'bz;  // Controlled_Buffer controlled_buffer_21
  assign out_7 = R10 ? register_11_q : 8'bz;  // Controlled_Buffer controlled_buffer_22
  assign out_7 = R11 ? register_12_q : 8'bz;  // Controlled_Buffer controlled_buffer_23
  assign controlled_buffer_24_out = R11 ? DataIn : 8'bz;  // Controlled_Buffer controlled_buffer_24
  Register register_12 (.D(controlled_buffer_24_out), .en(Read_Write), .Q(register_12_q), .clk(Clock), .clr(Clear));
  assign out_7 = R12 ? register_13_q : 8'bz;  // Controlled_Buffer controlled_buffer_25
  assign controlled_buffer_26_out = R12 ? DataIn : 8'bz;  // Controlled_Buffer controlled_buffer_26
  Register register_13 (.D(controlled_buffer_26_out), .en(Read_Write), .Q(register_13_q), .clk(Clock), .clr(Clear));
  Register register_14 (.D(controlled_buffer_27_out), .en(Read_Write), .Q(register_14_q), .clk(Clock), .clr(Clear));
  assign controlled_buffer_27_out = R13 ? DataIn : 8'bz;  // Controlled_Buffer controlled_buffer_27
  assign out_7 = R13 ? register_14_q : 8'bz;  // Controlled_Buffer controlled_buffer_28
  assign out_7 = R14 ? register_15_q : 8'bz;  // Controlled_Buffer controlled_buffer_29
  Register register_15 (.D(controlled_buffer_30_out), .en(Read_Write), .Q(register_15_q), .clk(Clock), .clr(Clear));
  assign controlled_buffer_30_out = R14 ? DataIn : 8'bz;  // Controlled_Buffer controlled_buffer_30
  Register register_16 (.D(controlled_buffer_31_out), .en(Read_Write), .Q(register_16_q), .clk(Clock), .clr(Clear));
  assign controlled_buffer_31_out = R15 ? DataIn : 8'bz;  // Controlled_Buffer controlled_buffer_31
  assign out_7 = R15 ? register_16_q : 8'bz;  // Controlled_Buffer controlled_buffer_32

  // Other names for the same wires on the sheet: CK = Clock; CL = Clear; IN[7:0] = DataIn; OT[7:0] = out_7;
  //   RW = Read_Write
endmodule

module MEM___IndexController (
  input  [7:0] Address,
  input  [7:0] Data,
  input  Enable,
  input  Clock,
  input  Clear,
  input  Store_Load,
  output [7:0] Out
);

  wire not_1_out;

  not not_1 (not_1_out, Store_Load);
  RAM #(.bus("separate")) ram_1 (
    .addr(Address), .din(Data), .data(Out), .str(not_1_out), .sel(Enable), .clk(Clock), .ld(Store_Load),
    .clr(Clear));
endmodule

module MEM (
  input  CR,
  input  Clock,
  input  Enable,
  input  [13:0] Data
);

  wire C0, C1, C2, C3, RR_W, SL;

  Demultiplexer #(.select(2), .disabled(0)) demultiplexer_1 (
    .out0(C0), .out1(C1), .out2(C2), .out3(C3), .in(1'b1), .sel(Data[13:12]), .en(Enable));
  MEM___RegisterController mem_registercontroller_1 (
    .Clock(Clock), .Clear(CR), .Read_Write(RR_W), .Enable(Enable));  // open: DataIn, out_7, Register
  MEM___IndexController mem_indexcontroller_1 (
    .Enable(Enable), .Clock(Clock), .Store_Load(SL), .Clear(CR));  // open: Address, Data, Out

  // Other names for the same wires on the sheet: CK = Clock; AD[7:0] = Data[7:0]; RG[3:0] = Data[11:8]; EN = Enable
endmodule
